// Logisim project Combinational_Logic_Blocks.circ as structural Verilog
module adder_1_bit (
  input  a,
  input  b,
  input  cin,
  output S,
  output Cout
);

  wire and_1_out, and_2_out, and_3_out;

  xor xor_1 (S, a, b, cin);
  and and_1 (and_1_out, a, b);
  and and_2 (and_2_out, a, cin);
  and and_3 (and_3_out, b, cin);
  or or_1 (Cout, and_1_out, and_2_out, and_3_out);
endmodule

module adder_4_bits (
  input  [3:0] A,
  input  [3:0] B,
  input  Cin,
  output [3:0] S,
  output Cout,
  output Overflow
);

  wire adder_1_bit_1_cout, adder_1_bit_2_cout, adder_1_bit_3_cout;

  adder_1_bit adder_1_bit_1 (.a(A[0]), .b(B[0]), .cin(Cin), .S(S[0]), .Cout(adder_1_bit_1_cout));
  adder_1_bit adder_1_bit_2 (.a(A[1]), .b(B[1]), .cin(adder_1_bit_1_cout), .S(S[1]), .Cout(adder_1_bit_2_cout));
  adder_1_bit adder_1_bit_3 (.a(A[2]), .b(B[2]), .cin(adder_1_bit_2_cout), .S(S[2]), .Cout(adder_1_bit_3_cout));
  adder_1_bit adder_1_bit_4 (.a(A[3]), .b(B[3]), .cin(adder_1_bit_3_cout), .S(S[3]), .Cout(Cout));
  xor xor_1 (Overflow, Cout, adder_1_bit_3_cout);
endmodule

module add_subtract_4_bits (
  input  [3:0] A,
  input  [3:0] B,
  input  Sub,
  output [3:0] S,
  output Cout,
  output Overflow
);

  wire adder_1_bit_1_cout, adder_1_bit_2_cout, adder_1_bit_3_cout, xor_1_out, xor_2_out, xor_3_out, xor_4_out;

  xor xor_1 (xor_1_out, Sub, B[0]);
  adder_1_bit adder_1_bit_1 (.a(A[0]), .b(xor_1_out), .cin(Sub), .S(S[0]), .Cout(adder_1_bit_1_cout));
  xor xor_2 (xor_2_out, B[1], Sub);
  adder_1_bit adder_1_bit_2 (.a(A[1]), .b(xor_2_out), .cin(adder_1_bit_1_cout), .S(S[1]), .Cout(adder_1_bit_2_cout));
  xor xor_3 (xor_3_out, B[2], Sub);
  adder_1_bit adder_1_bit_3 (.a(A[2]), .b(xor_3_out), .cin(adder_1_bit_2_cout), .S(S[2]), .Cout(adder_1_bit_3_cout));
  xor xor_4 (xor_4_out, B[3], Sub);
  adder_1_bit adder_1_bit_4 (.a(A[3]), .b(xor_4_out), .cin(adder_1_bit_3_cout), .S(S[3]), .Cout(Cout));
  xor xor_5 (Overflow, Cout, adder_1_bit_3_cout);
endmodule

module Branch (
  input  [3:0] A,
  input  [3:0] B,
  input  BrUn,
  output BrLT,
  output BrEq
);

  wire comparator_1_eq, comparator_1_lt, comparator_2_eq, comparator_2_lt;

  Comparator #(.width(4)) comparator_1 (.a(A), .b(B), .eq(comparator_1_eq), .lt(comparator_1_lt));  // open: gt
  Comparator #(.mode("unsigned"), .width(4)) comparator_2 (
    .a(A), .b(B), .eq(comparator_2_eq), .lt(comparator_2_lt));  // open: gt
  Multiplexer #(.enable("false")) multiplexer_1 (.in0(comparator_1_lt), .in1(comparator_2_lt), .out(BrLT), .sel(BrUn));
  Multiplexer #(.enable("false")) multiplexer_2 (.in0(comparator_1_eq), .in1(comparator_2_eq), .out(BrEq), .sel(BrUn));
endmodule

module Branch_details (
  input  [3:0] A,
  input  [3:0] B,
  input  BrUn,
  output BrLt,
  output BrEq
);

  wire and_1_out, and_2_out, and_3_out, and_4_out, and_5_out, and_6_out, and_7_out, and_8_out, and_9_out,
       and_10_out, and_11_out, and_12_out, and_13_out, and_14_out, and_15_out, and_16_out, and_17_out,
       and_18_out, and_19_out, and_20_out, and_21_out, and_22_out, and_23_out, and_24_out, and_25_out,
       and_26_out, and_27_out, and_28_out, and_29_out, and_30_out, and_31_out, and_32_out, not_1_out,
       not_2_out, not_3_out, not_4_out, not_5_out, not_6_out, not_7_out, not_8_out, not_9_out;

  not not_1 (not_1_out, A[3]);
  not not_2 (not_2_out, A[2]);
  not not_3 (not_3_out, A[1]);
  not not_4 (not_4_out, A[0]);
  not not_5 (not_5_out, B[3]);
  not not_6 (not_6_out, B[2]);
  not not_7 (not_7_out, B[1]);
  not not_8 (not_8_out, B[0]);
  not not_9 (not_9_out, BrUn);
  and and_1 (and_1_out, not_1_out, not_2_out, not_3_out, not_4_out, not_5_out, B[0]);
  and and_2 (and_2_out, not_1_out, not_2_out, not_3_out, not_5_out, B[1]);
  and and_3 (and_3_out, not_1_out, not_2_out, not_4_out, not_5_out, B[1], B[0]);
  and and_4 (and_4_out, not_1_out, not_2_out, not_5_out, B[2]);
  and and_5 (and_5_out, not_1_out, not_3_out, not_4_out, not_5_out, B[2], B[0]);
  and and_6 (and_6_out, not_1_out, not_3_out, not_5_out, B[2], B[1]);
  and and_7 (and_7_out, not_1_out, not_4_out, not_5_out, B[2], B[1], B[0]);
  and and_8 (and_8_out, not_1_out, B[3], BrUn);
  and and_9 (and_9_out, A[3], not_5_out, not_9_out);
  and and_10 (and_10_out, A[3], not_2_out, not_3_out, not_4_out, B[3], B[0]);
  and and_11 (and_11_out, A[3], not_2_out, not_3_out, B[3], B[1]);
  and and_12 (and_12_out, A[3], not_2_out, not_4_out, B[3], B[1], B[0]);
  and and_13 (and_13_out, A[3], not_2_out, B[3], B[2]);
  and and_14 (and_14_out, A[3], not_3_out, not_4_out, B[3], B[2], B[0]);
  and and_15 (and_15_out, A[3], not_3_out, B[3], B[2], B[1]);
  and and_16 (and_16_out, A[3], not_4_out, B[3], B[2], B[1], B[0]);
  and and_17 (and_17_out, not_1_out, not_2_out, not_3_out, not_4_out, not_5_out, not_6_out, not_7_out, not_8_out);
  and and_18 (and_18_out, not_1_out, not_2_out, not_3_out, A[0], not_5_out, not_6_out, not_7_out, B[0]);
  and and_19 (and_19_out, not_1_out, not_2_out, A[1], not_4_out, not_5_out, not_6_out, B[1], not_8_out);
  and and_20 (and_20_out, not_1_out, not_2_out, A[1], A[0], not_5_out, not_6_out, B[1], B[0]);
  and and_21 (and_21_out, not_1_out, A[2], not_3_out, not_4_out, not_5_out, B[2], not_7_out, not_8_out);
  and and_22 (and_22_out, not_1_out, A[2], not_3_out, A[0], not_5_out, B[2], not_7_out, B[0]);
  and and_23 (and_23_out, not_1_out, A[2], A[1], not_4_out, not_5_out, B[2], B[1], not_8_out);
  and and_24 (and_24_out, not_1_out, A[2], A[1], A[0], not_5_out, B[2], B[1], B[0]);
  and and_25 (and_25_out, A[3], not_2_out, not_3_out, not_4_out, B[3], not_6_out, not_7_out, not_8_out);
  and and_26 (and_26_out, A[3], not_2_out, not_3_out, A[0], B[3], not_6_out, not_7_out, B[0]);
  and and_27 (and_27_out, A[3], not_2_out, A[1], not_4_out, B[3], not_6_out, B[1], not_8_out);
  and and_28 (and_28_out, A[3], not_2_out, A[1], A[0], B[3], not_6_out, B[1], B[0]);
  and and_29 (and_29_out, A[3], A[2], not_3_out, not_4_out, B[3], B[2], not_7_out, not_8_out);
  and and_30 (and_30_out, A[3], A[2], not_3_out, A[0], B[3], B[2], not_7_out, B[0]);
  and and_31 (and_31_out, A[3], A[2], A[1], not_4_out, B[3], B[2], B[1], not_8_out);
  and and_32 (and_32_out, A[3], A[2], A[1], A[0], B[3], B[2], B[1], B[0]);
  or or_1 (BrLt, and_1_out, and_2_out, and_3_out, and_4_out, and_5_out, and_6_out, and_7_out, and_8_out, and_9_out, and_10_out, and_11_out, and_12_out, and_13_out, and_14_out, and_15_out, and_16_out);
  or or_2 (BrEq, and_17_out, and_18_out, and_19_out, and_20_out, and_21_out, and_22_out, and_23_out, and_24_out, and_25_out, and_26_out, and_27_out, and_28_out, and_29_out, and_30_out, and_31_out, and_32_out);
endmodule

module adder_1_bit_details (
  input  a,
  input  b,
  input  cin,
  output S,
  output Cout
);

  wire and_1_out, and_2_out, and_3_out, and_4_out, and_5_out, and_6_out, and_7_out, not_1_out, not_2_out,
       not_3_out;

  not not_1 (not_1_out, a);
  not not_2 (not_2_out, b);
  not not_3 (not_3_out, cin);
  and and_1 (and_1_out, not_1_out, not_2_out, cin);
  and and_2 (and_2_out, not_1_out, b, not_3_out);
  and and_3 (and_3_out, a, not_2_out, not_3_out);
  and and_4 (and_4_out, a, b, cin);
  and and_5 (and_5_out, b, cin);
  and and_6 (and_6_out, a, cin);
  and and_7 (and_7_out, a, b);
  or or_1 (S, and_1_out, and_2_out, and_3_out, and_4_out);
  or or_2 (Cout, and_5_out, and_6_out, and_7_out);
endmodule

module rv32_addr_decoder (
  input  [31:0] Inst,
  input  BrEq,
  input  BrLT,
  output R_Type,
  output ADD,
  output SUB,
  output BrUn
);

  wire and_2_out, not_1_out, not_2_out;
  wire [31:0] not_3_out;

  not not_1 (not_1_out, BrEq);
  not not_2 (not_2_out, BrLT);
  assign not_3_out = ~Inst;  // NOT_Gate not_3, 32 bits wide
  and and_1 (R_Type, not_3_out[2], not_3_out[3], Inst[4], Inst[5], not_3_out[6]);
  and and_2 (and_2_out, R_Type, not_3_out[12], not_3_out[13], not_3_out[14]);
  and and_3 (ADD, and_2_out, not_3_out[30]);
  and and_4 (SUB, and_2_out, Inst[30]);
  and and_5 (BrUn, not_3_out[2], not_3_out[3], not_3_out[4], Inst[5], Inst[6], Inst[30]);
endmodule

module ALU_4bit (
  input  [3:0] A,
  input  [3:0] B,
  input  [1:0] S,
  output Overflow,
  output [3:0] R
);

  wire [3:0] add_subtract_4_bits_1_s, and_1_out, multiplexer_1_out, or_1_out;

  // Probe on A
  // Probe on B
  assign and_1_out = A & B;  // AND_Gate and_1, 4 bits wide
  assign or_1_out = A | B;  // OR_Gate or_1, 4 bits wide
  add_subtract_4_bits add_subtract_4_bits_1 (
    .A(A), .B(B), .Sub(S[0]), .S(add_subtract_4_bits_1_s), .Overflow(Overflow));  // open: Cout
  Multiplexer #(.enable("false"), .width(4)) multiplexer_1 (
    .in0(and_1_out), .in1(or_1_out), .out(multiplexer_1_out), .sel(S[0]));
  Multiplexer #(.enable("false"), .width(4)) multiplexer_2 (
    .in0(add_subtract_4_bits_1_s), .in1(multiplexer_1_out), .out(R), .sel(S[1]));
  // Probe on R
endmodule

module mux2 (
  input  A,
  input  B,
  input  S,
  output C
);

  Multiplexer #(.enable("false")) multiplexer_1 (.in0(A), .in1(B), .out(C), .sel(S));
endmodule

module mux4 (
  input  A,
  input  B,
  input  C,
  input  D,
  input  [1:0] S,
  output E,
  output F
);

  wire multiplexer_1_out, multiplexer_2_out;

  // Probe on S
  Multiplexer #(.enable("false")) multiplexer_1 (.in0(A), .in1(B), .out(multiplexer_1_out), .sel(S[0]));
  Multiplexer #(.enable("false")) multiplexer_2 (.in0(C), .in1(D), .out(multiplexer_2_out), .sel(S[0]));
  Multiplexer #(.enable("false")) multiplexer_3 (.in0(multiplexer_1_out), .in1(multiplexer_2_out), .out(E), .sel(S[1]));
  Multiplexer #(.enable("false"), .select(2)) multiplexer_4 (.in0(A), .in1(B), .in2(C), .in3(D), .out(F), .sel(S));
endmodule

module mux2_basic (
  input  A,
  input  B,
  input  S,
  output C
);

  wire and_1_out, and_2_out;

  and and_1 (and_1_out, A, ~S);  // AND_Gate
  and and_2 (and_2_out, B, S);
  or or_1 (C, and_1_out, and_2_out);
endmodule

module rv32_control_CL (
  input  [31:0] Inst,
  input  BrEq,
  input  BrLT,
  output BrUn,
  output MemRW,
  output BSel,
  output [3:0] ALUSel
);

  wire and_2_out, and_4_out;

  and and_1 (BrUn, Inst[13], Inst[6], Inst[5]);
  // Probe on and_2_out
  and and_2 (and_2_out, Inst[1], Inst[0]);
  and and_3 (MemRW, ~Inst[6], Inst[5], ~Inst[4], ~Inst[3], ~Inst[2], and_2_out);  // AND_Gate
  and and_4 (and_4_out, and_2_out, ~Inst[6], Inst[5], Inst[4], ~Inst[3], ~Inst[2]);  // AND_Gate
  not not_1 (BSel, and_4_out);
  Multiplexer #(.enable("false"), .width(4)) multiplexer_1 (
    .in0({Inst[14:12], Inst[30]}), .in1(4'b0000), .out(ALUSel), .sel(BSel));
endmodule

module rv32_control_ROM (
  input  [31:0] Inst,
  input  BrEq,
  input  BrLT,
  output PCSel,
  output [2:0] ImmSel,
  output BrUn,
  output Asel,
  output BSel,
  output [3:0] ALUSel,
  output MemRW,
  output RegWEn,
  output [1:0] WBSel
);

  // Probe on {BrEq, BrLT, Inst[30], Inst[14:12], Inst[6:2]}
  ROM #(.addrWidth(11), .dataWidth(15)) rom_1 (
    .addr({BrEq, BrLT, Inst[30], Inst[14:12], Inst[6:2]}),
    .data({PCSel, ImmSel, BrUn, Asel, BSel, ALUSel, MemRW, RegWEn, WBSel}));
  // Probe on {PCSel, ImmSel, BrUn, Asel, BSel, ALUSel, MemRW, RegWEn, WBSel}

  // Notes on the sheet:
  //   contents of rom_1 (hex, n*v repeats v):
  //   4*0 105 7*0 5 11*0 2300 19*0 25 19*0 104 7*0 908 195*0 15 255*0 5 255*0 15 255*0 5 11*0 5300 243*0
  //   15 255*0 5 255*0 15
endmodule
